// Logisim project TallerLogica-Combinatorios.circ as structural Verilog: 9 circuits, main circuit verificador
module sumador_simple (
  input  A,
  input  B,
  output S,
  output Cout
);

  xor xor_1 (S, A, B);
  and and_1 (Cout, A, B);
endmodule

module sumador_completo (
  input  A,
  input  B,
  input  Cin,
  output Cout,
  output S
);

  wire sumador_simple_1_cout, sumador_simple_1_s, sumador_simple_2_cout;

  sumador_simple sumador_simple_1 (.A(A), .B(B), .S(sumador_simple_1_s), .Cout(sumador_simple_1_cout));
  or or_1 (Cout, sumador_simple_1_cout, sumador_simple_2_cout);
  sumador_simple sumador_simple_2 (.A(sumador_simple_1_s), .B(Cin), .S(S), .Cout(sumador_simple_2_cout));
endmodule

module sumador_4 (
  input  Cin,
  input  [3:0] A,
  input  [3:0] B,
  output [3:0] S,
  output Cout
);

  wire sumador_completo_1_cout, sumador_completo_2_cout, sumador_completo_3_cout;

  sumador_completo sumador_completo_1 (.A(A[0]), .B(B[0]), .Cin(Cin), .Cout(sumador_completo_1_cout), .S(S[0]));
  sumador_completo sumador_completo_2 (
    .A(A[1]), .B(B[1]), .Cin(sumador_completo_1_cout), .Cout(sumador_completo_2_cout), .S(S[1]));
  sumador_completo sumador_completo_3 (
    .A(A[2]), .B(B[2]), .Cin(sumador_completo_2_cout), .Cout(sumador_completo_3_cout), .S(S[2]));
  sumador_completo sumador_completo_4 (.A(A[3]), .B(B[3]), .Cin(sumador_completo_3_cout), .Cout(Cout), .S(S[3]));
  Hex_Digit_Display hex_digit_display_1 (.value(S));  // open: dp
endmodule

module comparador_cero (
  input  [3:0] A,
  output Z
);

  wire or_1_out, or_2_out, or_3_out;

  or or_1 (or_1_out, A[0], A[1]);
  or or_2 (or_2_out, A[2], A[3]);
  or or_3 (or_3_out, or_1_out, or_2_out);
  not not_1 (Z, or_3_out);
endmodule

module sumador_flags (
  input  Cin,
  input  [3:0] A,
  input  [3:0] B,
  output [3:0] S,
  output N,
  output Z,
  output V,
  output C
);

  wire not_1_out, xor_1_out, xor_2_out;

  xor xor_1 (xor_1_out, A[3], B[3]);
  not not_1 (not_1_out, xor_1_out);
  xor xor_2 (xor_2_out, N, B[3]);
  sumador_4 sumador_4_1 (.Cin(Cin), .A(A), .B(B), .S({N, S[2:0]}), .Cout(C));
  and and_1 (V, not_1_out, xor_2_out);
  Hex_Digit_Display hex_digit_display_1 (.value({N, S[2:0]}));  // open: dp
  comparador_cero comparador_cero_1 (.A({N, S[2:0]}), .Z(Z));

  assign S[3] = N;
endmodule

module incrementador_4 (
  input  [3:0] A,
  output [3:0] S
);

  sumador_4 sumador_4_1 (.Cin(1'b1), .A(A), .S(S));  // open: B, Cout
  Hex_Digit_Display hex_digit_display_1 (.value(S));  // open: dp
endmodule

module inversor_4 (
  input  [3:0] A,
  input  INV,
  output [3:0] S
);

  wire [3:0] incrementador_4_1_s, not_1_out;

  not not_1 (not_1_out[0], A[0]);
  not not_2 (not_1_out[1], A[1]);
  not not_3 (not_1_out[2], A[2]);
  not not_4 (not_1_out[3], A[3]);
  incrementador_4 incrementador_4_1 (.A(not_1_out), .S(incrementador_4_1_s));
  Multiplexer #(.width(4)) multiplexer_1 (.in0(A), .in1(incrementador_4_1_s), .out(S), .sel(INV));
  Hex_Digit_Display hex_digit_display_1 (.value(S));  // open: dp
endmodule

module ALU (
  input  [3:0] A,
  input  [3:0] B,
  input  [1:0] OP,
  output N,
  output Z,
  output V,
  output C,
  output [3:0] S
);

  wire and_5_out, and_6_out, comparador_cero_1_z, decoder_1_out1, not_1_out, not_2_out, not_3_out, not_4_out,
       not_5_out, sumador_flags_1_c, sumador_flags_1_v, xor_1_out, xor_2_out;
  wire [3:0] and_1_out, inversor_4_1_s, or_1_out, sumador_flags_1_s;

  Decoder #(.select(2)) decoder_1 (.out1(decoder_1_out1), .sel(OP));  // open: out0, out2, out3, en
  not not_1 (not_1_out, B[3]);
  inversor_4 inversor_4_1 (.A(B), .INV(decoder_1_out1), .S(inversor_4_1_s));
  and and_1 (and_1_out[0], B[0], A[0]);
  and and_2 (and_1_out[1], B[1], A[1]);
  and and_3 (and_1_out[2], B[2], A[2]);
  and and_4 (and_1_out[3], B[3], A[3]);
  or or_1 (or_1_out[0], A[0], B[0]);
  or or_2 (or_1_out[1], A[1], B[1]);
  or or_3 (or_1_out[2], A[2], B[2]);
  or or_4 (or_1_out[3], A[3], B[3]);
  xor xor_1 (xor_1_out, A[3], not_1_out);
  not not_2 (not_2_out, xor_1_out);
  xor xor_2 (xor_2_out, not_1_out, N);
  and and_5 (and_5_out, not_2_out, xor_2_out);
  comparador_cero comparador_cero_1 (.A(B), .Z(comparador_cero_1_z));
  sumador_flags sumador_flags_1 (
    .A(A), .B(inversor_4_1_s), .S(sumador_flags_1_s), .V(sumador_flags_1_v), .C(sumador_flags_1_c));  // open: Cin, N, Z
  Multiplexer #(.select(2), .width(4)) multiplexer_1 (
    .in0(sumador_flags_1_s), .in1(sumador_flags_1_s), .in2(and_1_out), .in3(or_1_out), .out({N, S[2:0]}),
    .sel(OP));
  not not_3 (not_3_out, 1'b1);
  Hex_Digit_Display hex_digit_display_1 (.value({N, S[2:0]}));  // open: dp
  comparador_cero comparador_cero_2 (.A({N, S[2:0]}), .Z(Z));
  not not_4 (not_4_out, sumador_flags_1_c);
  not not_5 (not_5_out, comparador_cero_1_z);
  Multiplexer #(.select(2)) multiplexer_2 (
    .in0(sumador_flags_1_v), .in1(and_5_out), .in2(not_3_out), .in3(not_3_out), .out(V), .sel(OP));
  Multiplexer #(.select(2)) multiplexer_3 (
    .in0(sumador_flags_1_c), .in1(and_6_out), .in2(not_3_out), .in3(not_3_out), .out(C), .sel(OP));
  and and_6 (and_6_out, not_4_out, not_5_out);

  assign S[3] = N;
endmodule

module verificador (
  output [3:0] out_1,
  output [3:0] out_2,
  output [1:0] out_3,
  output halt,
  output N,
  output Z,
  output V,
  output C,
  output [3:0] res
);

  wire clock_1_out;

  Clock clock_1 (.out(clock_1_out));
  Counter #(.max('h3ff), .width(10)) counter_1 (
    .clk(clock_1_out), .carry(halt), .Q({out_3, out_2, out_1}));  // open: clr, load, up, count, D
  ALU alu_1 (.A(out_1), .B(out_2), .OP(out_3), .N(N), .Z(Z), .V(V), .C(C), .S(res));
endmodule
