// Logisim project taller3.circ as structural Verilog: 7 circuits, main circuit Ejercicio1
module Ejercicio1 (
  input  reset,
  output Q1,
  output Q0
);

  wire and_1_out, clock_1_out, d_ff_2_qn;

  Clock clock_1 (.out(clock_1_out));
  and and_1 (and_1_out, Q1, d_ff_2_qn);
  D_Flip_Flop d_ff_1 (.D(d_ff_2_qn), .clk(clock_1_out), .Q(Q1), .reset(reset));  // open: Qn, preset
  D_Flip_Flop d_ff_2 (.D(and_1_out), .clk(clock_1_out), .Q(Q0), .Qn(d_ff_2_qn), .preset(reset));  // open: reset
endmodule

module Contador2B (
  input  Clock,
  output Q1,
  output Q0
);

  J_K_Flip_Flop j_k_ff_1 (.J(1'b1), .K(1'b1), .clk(Clock), .Q(Q0));  // open: Qn, preset, reset
  J_K_Flip_Flop j_k_ff_2 (.J(Q0), .K(Q0), .clk(Clock), .Q(Q1));  // open: Qn, preset, reset
endmodule

module Ejercicio3 (
  output out_1,
  output out_2
);

  wire clock_1_out, contador2b_1_q0, contador2b_1_q1, not_1_out;

  Clock clock_1 (.out(clock_1_out));
  Contador2B contador2b_1 (.Clock(clock_1_out), .Q1(contador2b_1_q1), .Q0(contador2b_1_q0));
  not not_1 (not_1_out, contador2b_1_q0);
  or or_1 (out_1, contador2b_1_q1, contador2b_1_q0);
  and and_1 (out_2, not_1_out, contador2b_1_q1);
endmodule

module Ejercicio4 (
  input  Neg,
  output out_2,
  output out_3
);

  wire and_1_out, clock_1_out, contador2b_1_q0, contador2b_1_q1, not_1_out, or_1_out;

  Clock clock_1 (.out(clock_1_out));
  Contador2B contador2b_1 (.Clock(clock_1_out), .Q1(contador2b_1_q1), .Q0(contador2b_1_q0));
  not not_1 (not_1_out, contador2b_1_q0);
  or or_1 (or_1_out, contador2b_1_q1, contador2b_1_q0);
  and and_1 (and_1_out, not_1_out, contador2b_1_q1);
  xor xor_1 (out_2, or_1_out, Neg);
  xor xor_2 (out_3, and_1_out, Neg);
endmodule

module Ejercicio5a (
  input  reset,
  output Q1,
  output Q0
);

  wire and_1_out, clock_1_out, d_ff_1_q, d_ff_2_q, d_ff_2_qn, xor_1_out;

  Clock clock_1 (.out(clock_1_out));
  and and_1 (and_1_out, d_ff_1_q, d_ff_2_qn);
  D_Flip_Flop d_ff_1 (.D(d_ff_2_qn), .clk(clock_1_out), .Q(d_ff_1_q), .Qn(Q1), .reset(reset));  // open: preset
  D_Flip_Flop d_ff_2 (.D(and_1_out), .clk(clock_1_out), .Q(d_ff_2_q), .Qn(d_ff_2_qn), .preset(reset));  // open: reset
  not not_1 (Q0, xor_1_out);
  xor xor_1 (xor_1_out, d_ff_1_q, d_ff_2_q);
endmodule

module Ejercicio5b (
  output out_1,
  output out_2
);

  wire clock_1_out, contador2b_1_q0, contador2b_1_q1, not_1_out;

  Clock clock_1 (.out(clock_1_out));
  Contador2B contador2b_1 (.Clock(clock_1_out), .Q1(contador2b_1_q1), .Q0(contador2b_1_q0));
  not not_1 (not_1_out, contador2b_1_q1);
  or or_1 (out_1, not_1_out, contador2b_1_q0);
  not not_2 (out_2, contador2b_1_q0);
endmodule

module Ejercicio5c (
  input  NEG,
  output out_2,
  output out_3
);

  wire clock_1_out, contador2b_1_q0, contador2b_1_q1, not_1_out, not_2_out, or_1_out;

  Clock clock_1 (.out(clock_1_out));
  not not_1 (not_1_out, contador2b_1_q1);
  Contador2B contador2b_1 (.Clock(clock_1_out), .Q1(contador2b_1_q1), .Q0(contador2b_1_q0));
  not not_2 (not_2_out, contador2b_1_q0);
  or or_1 (or_1_out, not_1_out, contador2b_1_q0);
  xor xor_1 (out_2, or_1_out, NEG);
  xor xor_2 (out_3, not_2_out, NEG);
endmodule
