// Logisim project taller3.circ as structural Verilog: 9 circuits, main circuit main
module main (
  input  RESET,
  output o1,
  output o0
);

  wire and_1_out, clock_1_out, d_ff_2_qn;

  Clock clock_1 (.out(clock_1_out));
  D_Flip_Flop d_ff_1 (.D(d_ff_2_qn), .clk(clock_1_out), .Q(o1), .reset(RESET));  // open: Qn, preset
  D_Flip_Flop d_ff_2 (.D(and_1_out), .clk(clock_1_out), .Q(o0), .Qn(d_ff_2_qn), .preset(RESET));  // open: reset
  and and_1 (and_1_out, o1, d_ff_2_qn);
endmodule

module contador2b (
  input  in_1,
  output o0,
  output o1
);

  J_K_Flip_Flop Q0 (.J(1'b1), .K(1'b1), .clk(in_1), .Q(o0));  // open: Qn, preset, reset
  J_K_Flip_Flop Q1 (.J(o0), .K(o0), .clk(in_1), .Q(o1));  // open: Qn, preset, reset
endmodule

module ejer3 (
  input  in_1,
  output o0,
  output o1
);

  wire contador2b_1_o0, contador2b_1_o1, not_1_out;

  contador2b contador2b_1 (.in_1(in_1), .o0(contador2b_1_o0), .o1(contador2b_1_o1));
  not not_1 (not_1_out, contador2b_1_o0);
  or or_1 (o0, contador2b_1_o0, contador2b_1_o1);
  and and_1 (o1, not_1_out, contador2b_1_o1);
endmodule

module ejer3bis (
  input  pulsador,
  input  NEG,
  output o0,
  output o1
);

  wire ejer3_1_o0, ejer3_1_o1;

  ejer3 ejer3_1 (.in_1(pulsador), .o0(ejer3_1_o0), .o1(ejer3_1_o1));
  xor xor_1 (o0, ejer3_1_o0, NEG);
  xor xor_2 (o1, ejer3_1_o1, NEG);
endmodule

module Bejer1 (
  input  RESET,
  output o1,
  output o0
);

  wire clock_1_out, d_ff_1_q, d_ff_2_q, d_ff_2_qn, xor_1_out;

  Clock clock_1 (.out(clock_1_out));
  D_Flip_Flop d_ff_1 (.D(o1), .clk(clock_1_out), .Q(d_ff_1_q), .Qn(o1), .reset(RESET));  // open: preset
  D_Flip_Flop d_ff_2 (.D(o0), .clk(clock_1_out), .Q(d_ff_2_q), .Qn(d_ff_2_qn), .preset(RESET));  // open: reset
  xor xor_1 (xor_1_out, d_ff_2_q, d_ff_1_q);
  not not_1 (o0, xor_1_out);
endmodule

module Bejer1bien (
  input  RESET,
  output o1,
  output o0
);

  wire and_1_out, clock_1_out, d_ff_1_q, d_ff_2_q, d_ff_2_qn, xor_1_out;

  Clock clock_1 (.out(clock_1_out));
  D_Flip_Flop d_ff_1 (.D(d_ff_2_qn), .clk(clock_1_out), .Q(d_ff_1_q), .reset(RESET));  // open: Qn, preset
  D_Flip_Flop d_ff_2 (.D(and_1_out), .clk(clock_1_out), .Q(d_ff_2_q), .Qn(d_ff_2_qn), .preset(RESET));  // open: reset
  and and_1 (and_1_out, d_ff_1_q, d_ff_2_qn);
  xor xor_1 (xor_1_out, d_ff_2_q, d_ff_1_q);
  not not_1 (o1, d_ff_1_q);
  not not_2 (o0, xor_1_out);
endmodule

module Bejer3 (
  input  in_1,
  output out_2,
  output out_3
);

  wire ejer3_1_o0, ejer3_1_o1;

  ejer3 ejer3_1 (.in_1(in_1), .o0(ejer3_1_o0), .o1(ejer3_1_o1));
  traductor traductor_1 (.o1prev(ejer3_1_o1), .o0prev(ejer3_1_o0), .o1(out_2), .o0(out_3));
endmodule

module traductor (
  input  o1prev,
  input  o0prev,
  output o1,
  output o0
);

  wire xor_1_out;

  not not_1 (o1, o1prev);
  xor xor_1 (xor_1_out, o0prev, o1prev);
  not not_2 (o0, xor_1_out);
endmodule

module Bejer3bis (
  input  pulsador,
  input  NEG,
  output o0,
  output o1
);

  wire bejer3_1_out_2, bejer3_1_out_3;

  Bejer3 bejer3_1 (.in_1(pulsador), .out_2(bejer3_1_out_2), .out_3(bejer3_1_out_3));
  xor xor_1 (o0, bejer3_1_out_2, NEG);
  xor xor_2 (o1, bejer3_1_out_3, NEG);
endmodule
